# Fritzing sketch breadboard (saved by Fritzing 0.9.3b)
breadboards: 3

parts:
  Part1 = Arduino Nano (Rev3.0)  # not connected
  S1 = Tactile Switch Buttons - 12mm Square [package=tactile-pth-12mm]
  S2 = Tactile Switch Buttons - 12mm Square [package=tactile-pth-12mm]
  S3 = Tactile Switch Buttons - 12mm Square [package=tactile-pth-12mm]
  S4 = Tactile Switch Buttons - 12mm Square [package=tactile-pth-12mm]
  S5 = Tactile Switch Buttons - 12mm Square [package=tactile-pth-12mm]
  S6 = Tactile Switch Buttons - 12mm Square [package=tactile-pth-12mm]
  U1 = POT [package=pot_alpha_rv16af-20]  # not connected
  U2 = POT [package=pot_alpha_rv16af-20]  # not connected
  U3 = POT [package=pot_alpha_rv16af-20]  # not connected
  U4 = POT [package=pot_alpha_rv16af-20]  # not connected
  LED1 = LED - 5mm [color="Red (633nm)" package="5 mm [THT]"]  # not connected
  U5 = MIDI_CONN_FEMALE [package=din_5_female]  # not connected
  U6 = MIDI_CONN_FEMALE [package=din_5_female]  # not connected

nets:
  N1: S1.1, S1.3
  N2: S1.2, S1.4
  N3: S2.1, S2.3
  N4: S2.2, S2.4
  N5: S3.1, S3.3
  N6: S3.2, S3.4
  N7: S4.1, S4.3
  N8: S4.2, S4.4
  N9: S5.1, S5.3
  N10: S5.2, S5.4
  N11: S6.1, S6.3
  N12: S6.2, S6.4

custom parts:
  Tactile Switch Buttons - 12mm Square: Medium-sized clicky momentary switches are standard input "buttons" on electronic projects. These work best in a PCB but can be used on a solderless breadboard as shown in this tutorial. The pins are normally open (disconnected) and when the button is pressed they are momentarily closed. They come in a pack of 10, they're pretty handy so you'll want to keep them around. You can find an EAGLE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
